# Fritzing sketch GPIO Switches (saved by Fritzing 0.9.2b)
breadboards: 1

parts:
  FET1 = STP16NF06 N-Channel Power MOSFET
  R1 = Resistor [tolerance=±5% resistance=4.7k package=THT]
  Raspberry_Pi1 = Raspberry Pi 2
  FET2 = STP16NF06 N-Channel Power MOSFET
  R2 = Resistor [tolerance=±5% resistance=4.7k package=THT]
  Part1 = Humidity Temperature Sensor SHT15

nets:
  N1: FET1.gate, R1.Pin_1, Raspberry_Pi1.GPIO17
  GND: FET1.source, R1.Pin_0, Raspberry_Pi1.GND, FET2.source, R2.Pin_0, Part1.GND
  3V3: Raspberry_Pi1.3v3, Part1.VCC
  N2: Raspberry_Pi1.GPIO2, Part1.SDA
  N3: Raspberry_Pi1.GPIO3, Part1.SCL
  N4: Raspberry_Pi1.GPIO27, FET2.gate, R2.Pin_1

custom parts:
  STP16NF06 N-Channel Power MOSFET: STP16NF06 N-channel Power MOSFET
